// Logisim project control-logic.circ as structural Verilog: 9 circuits, main circuit control_logic
module control_logic (
  input  [31:0] inst,
  input  BrEq,
  input  BrLt,
  output [1:0] PCSel,
  output RegWEn,
  output [2:0] ImmSel,
  output BrUn,
  output [1:0] ASel,
  output [1:0] BSel,
  output [3:0] ALUSel,
  output MemRW,
  output [1:0] WBSel,
  output CSRSel,
  output CSRWen
);

  wire [3:0] alu_op_imm, alu_op_reg, bit_extender_1_out, multiplexer_3_out, opcode_type;

  op_type op_type_1 (.Opcode(inst[6:0]), .opcode_type(opcode_type));
  Imm imm_1 (.opcode_type(opcode_type), .ImmSel(ImmSel));
  Mem mem_1 (.opcode_type(opcode_type), .MemRW(MemRW), .RegWEn(RegWEn));
  ABSel absel_1 (.opcode_type(opcode_type), .ASel(ASel), .BSel(BSel));
  WB wb_1 (.opcode_type(opcode_type), .WBSel(WBSel));
  Multiplexer #(.enable("false"), .select(4), .width(4)) multiplexer_1 (
    .in0(alu_op_reg), .in1(4'b0000), .in2(alu_op_imm), .in3(4'b0000), .in4(4'b0000), .in5(4'b0000),
    .in6(4'b0000), .in7(4'b0000), .in8(4'b0000), .in9(4'b0000), .in10(4'b0000), .out(ALUSel),
    .sel(opcode_type));  // open: in11, in12, in13, in14, in15
  Multiplexer #(.enable("false"), .select(3), .width(4)) multiplexer_2 (
    .in0(bit_extender_1_out), .in1(bit_extender_1_out), .in2(bit_extender_1_out), .in3(bit_extender_1_out),
    .in4(bit_extender_1_out), .in5({inst[30], inst[14:12]}), .in6(bit_extender_1_out),
    .in7(bit_extender_1_out), .out(alu_op_imm), .sel(inst[14:12]));
  assign bit_extender_1_out = {{1{1'b0}}, inst[14:12]};  // Bit_Extender bit_extender_1
  Branch branch_1 (
    .opcode_type(opcode_type), .funct3(inst[14:12]), .BrEq(BrEq), .BrLt(BrLt), .BrUn(BrUn), .PCSel(PCSel));
  CSR csr_1 (.opcode_type(opcode_type), .funct3(inst[14:12]), .CSRWen(CSRWen), .CSRSel(CSRSel));
  Multiplexer #(.enable("false"), .select(2), .width(4)) multiplexer_3 (
    .in0(4'b0000), .in1(4'b1000), .in2(4'b1100), .out(multiplexer_3_out), .sel({inst[30], inst[25]}));  // open: in3
  Multiplexer #(.enable("false"), .select(3), .width(4)) multiplexer_4 (
    .in0(multiplexer_3_out), .in1({inst[25], inst[14:12]}), .in2(alu_op_imm), .in3({inst[25], inst[14:12]}),
    .in4(alu_op_imm), .in5(alu_op_imm), .in6(alu_op_imm), .in7(alu_op_imm), .out(alu_op_reg),
    .sel(inst[14:12]));

  // Other names for the same wires on the sheet: Opcode[6:0] = inst[6:0]; opcode_t[6:0] = inst[6:0];
  //   rd[4:0] = inst[11:7]; funct3[2:0] = inst[14:12]; funct3_imm[3:0] = {inst[30], inst[14:12]};
  //   funct3_reg[3:0] = {inst[25], inst[14:12]}; rs1[4:0] = inst[19:15]; rs2[4:0] = inst[24:20];
  //   funct7[6:0] = inst[31:25]; funct7_new[1:0] = {inst[30], inst[25]}

  // Notes on the sheet:
  //   INPUTS to your circuit
  //   DON'T CHANGE THE LOCATIONS OF THE INPUTS AND OUTPUTS!
  //   OUTPUT from your circuit
endmodule

module op_type (
  input  [6:0] Opcode,
  output [3:0] opcode_type
);

  wire comparator_1_eq, comparator_2_eq, comparator_3_eq, comparator_4_eq, comparator_5_eq, comparator_6_eq,
       comparator_7_eq, comparator_8_eq, comparator_9_eq, comparator_10_eq;
  wire [3:0] multiplexer_1_out, multiplexer_2_out, multiplexer_3_out, multiplexer_4_out, multiplexer_5_out,
       multiplexer_6_out, multiplexer_7_out, multiplexer_8_out, multiplexer_9_out;

  Comparator #(.mode("unsigned"), .width(7)) comparator_1 (
    .a(Opcode), .b(7'b0110011), .eq(comparator_1_eq));  // open: gt, lt
  Comparator #(.mode("unsigned"), .width(7)) comparator_2 (
    .a(Opcode), .b(7'b0000011), .eq(comparator_2_eq));  // open: gt, lt
  Comparator #(.mode("unsigned"), .width(7)) comparator_3 (
    .a(Opcode), .b(7'b0010011), .eq(comparator_3_eq));  // open: gt, lt
  Comparator #(.mode("unsigned"), .width(7)) comparator_4 (
    .a(Opcode), .b(7'b0100011), .eq(comparator_4_eq));  // open: gt, lt
  Comparator #(.mode("unsigned"), .width(7)) comparator_5 (
    .a(Opcode), .b(7'b1100011), .eq(comparator_5_eq));  // open: gt, lt
  Comparator #(.mode("unsigned"), .width(7)) comparator_6 (
    .a(Opcode), .b(7'b0010111), .eq(comparator_6_eq));  // open: gt, lt
  Comparator #(.mode("unsigned"), .width(7)) comparator_7 (
    .a(Opcode), .b(7'b0110111), .eq(comparator_7_eq));  // open: gt, lt
  Comparator #(.mode("unsigned"), .width(7)) comparator_8 (
    .a(Opcode), .b(7'b1101111), .eq(comparator_8_eq));  // open: gt, lt
  Comparator #(.mode("unsigned"), .width(7)) comparator_9 (
    .a(Opcode), .b(7'b1100111), .eq(comparator_9_eq));  // open: gt, lt
  Comparator #(.mode("unsigned"), .width(7)) comparator_10 (
    .a(Opcode), .b(7'b1110011), .eq(comparator_10_eq));  // open: gt, lt
  Multiplexer #(.enable("false"), .width(4)) multiplexer_1 (
    .in0(4'b1010), .in1(4'b0000), .out(multiplexer_1_out), .sel(comparator_1_eq));
  Multiplexer #(.enable("false"), .width(4)) multiplexer_2 (
    .in0(multiplexer_1_out), .in1(4'b0001), .out(multiplexer_2_out), .sel(comparator_2_eq));
  Multiplexer #(.enable("false"), .width(4)) multiplexer_3 (
    .in0(multiplexer_2_out), .in1(4'b0010), .out(multiplexer_3_out), .sel(comparator_3_eq));
  Multiplexer #(.enable("false"), .width(4)) multiplexer_4 (
    .in0(multiplexer_3_out), .in1(4'b0011), .out(multiplexer_4_out), .sel(comparator_4_eq));
  Multiplexer #(.enable("false"), .width(4)) multiplexer_5 (
    .in0(multiplexer_4_out), .in1(4'b0100), .out(multiplexer_5_out), .sel(comparator_5_eq));
  Multiplexer #(.enable("false"), .width(4)) multiplexer_6 (
    .in0(multiplexer_5_out), .in1(4'b0101), .out(multiplexer_6_out), .sel(comparator_6_eq));
  Multiplexer #(.enable("false"), .width(4)) multiplexer_7 (
    .in0(multiplexer_6_out), .in1(4'b0110), .out(multiplexer_7_out), .sel(comparator_7_eq));
  Multiplexer #(.enable("false"), .width(4)) multiplexer_8 (
    .in0(multiplexer_7_out), .in1(4'b0111), .out(multiplexer_8_out), .sel(comparator_8_eq));
  Multiplexer #(.enable("false"), .width(4)) multiplexer_9 (
    .in0(multiplexer_8_out), .in1(4'b1000), .out(multiplexer_9_out), .sel(comparator_9_eq));
  Multiplexer #(.enable("false"), .width(4)) multiplexer_10 (
    .in0(multiplexer_9_out), .in1(4'b1001), .out(opcode_type), .sel(comparator_10_eq));

  // Notes on the sheet:
  //   INPUT
  //   OUTPUT
endmodule

module Imm (
  input  [3:0] opcode_type,
  output [2:0] ImmSel
);

  Multiplexer #(.enable("false"), .select(4), .width(3)) multiplexer_1 (
    .in0(3'b000), .in1(3'b000), .in2(3'b000), .in3(3'b001), .in4(3'b010), .in5(3'b011), .in6(3'b011),
    .in7(3'b100), .in8(3'b000), .in9(3'b000), .in10(3'b000), .out(ImmSel), .sel(opcode_type));  // open: in11, in12, in13, in14, in15

  // Notes on the sheet:
  //   INPUT
  //   OUTPUT
endmodule

module ALU (
  input  [3:0] opcode_type,
  input  [2:0] funct3,
  input  [6:0] funct7,
  output [3:0] ALUSel
);

  wire ALUSel_0, ALUSel_1, ALUSel_2, ALUSel_4, ALUSel_5, ALUSel_6, ALUSel_7, ALUSel_8, ALUSel_9, ALUSel_11,
       ALUSel_12, ALUSel_13, comparator_1_eq, comparator_2_eq, comparator_3_eq, comparator_4_eq,
       comparator_5_eq, comparator_6_eq, comparator_7_eq, comparator_8_eq, comparator_9_eq, comparator_10_eq,
       comparator_11_eq, comparator_12_eq, comparator_13_eq, comparator_14_eq, comparator_15_eq,
       comparator_16_eq, comparator_17_eq, comparator_18_eq, comparator_19_eq;
  wire [3:0] ALUSel_imm, ALUSel_type0, ALUSel_type1, funct3_type, multiplexer_2_out, multiplexer_3_out,
       multiplexer_4_out, multiplexer_5_out, multiplexer_6_out, multiplexer_7_out, multiplexer_8_out;

  Comparator #(.mode("unsigned"), .width(3)) comparator_1 (
    .a(funct3), .b(3'b000), .eq(comparator_1_eq));  // open: gt, lt
  Comparator #(.mode("unsigned"), .width(3)) comparator_2 (
    .a(funct3), .b(3'b001), .eq(comparator_2_eq));  // open: gt, lt
  Comparator #(.mode("unsigned"), .width(3)) comparator_3 (
    .a(funct3), .b(3'b010), .eq(comparator_3_eq));  // open: gt, lt
  Comparator #(.mode("unsigned"), .width(3)) comparator_4 (
    .a(funct3), .b(3'b011), .eq(comparator_4_eq));  // open: gt, lt
  Comparator #(.mode("unsigned"), .width(3)) comparator_5 (
    .a(funct3), .b(3'b100), .eq(comparator_5_eq));  // open: gt, lt
  Comparator #(.mode("unsigned"), .width(3)) comparator_6 (
    .a(funct3), .b(3'b101), .eq(comparator_6_eq));  // open: gt, lt
  Comparator #(.mode("unsigned"), .width(3)) comparator_7 (
    .a(funct3), .b(3'b110), .eq(comparator_7_eq));  // open: gt, lt
  Comparator #(.mode("unsigned"), .width(3)) comparator_8 (
    .a(funct3), .b(3'b111), .eq(comparator_8_eq));  // open: gt, lt
  Comparator #(.mode("unsigned"), .width(4)) comparator_9 (
    .a({funct7[5:3], funct7[0]}), .b(4'b0000), .eq(comparator_9_eq));  // open: gt, lt
  Comparator #(.mode("unsigned"), .width(4)) comparator_10 (
    .a(funct3_type), .b(4'b0000), .eq(comparator_10_eq));  // open: gt, lt
  Comparator #(.mode("unsigned"), .width(4)) comparator_11 (
    .a({funct7[5:3], funct7[0]}), .b(4'b0001), .eq(comparator_11_eq));  // open: gt, lt
  Comparator #(.mode("unsigned"), .width(4)) comparator_12 (
    .a({funct7[5:3], funct7[0]}), .b(4'b1000), .eq(comparator_12_eq));  // open: gt, lt
  Comparator #(.mode("unsigned"), .width(4)) comparator_13 (
    .a(funct3_type), .b(4'b0001), .eq(comparator_13_eq));  // open: gt, lt
  Comparator #(.mode("unsigned"), .width(4)) comparator_14 (
    .a(funct3_type), .b(4'b0010), .eq(comparator_14_eq));  // open: gt, lt
  Comparator #(.mode("unsigned"), .width(4)) comparator_15 (
    .a(funct3_type), .b(4'b0011), .eq(comparator_15_eq));  // open: gt, lt
  Comparator #(.mode("unsigned"), .width(4)) comparator_16 (
    .a(funct3_type), .b(4'b0100), .eq(comparator_16_eq));  // open: gt, lt
  Comparator #(.mode("unsigned"), .width(4)) comparator_17 (
    .a(funct3_type), .b(4'b0101), .eq(comparator_17_eq));  // open: gt, lt
  Comparator #(.mode("unsigned"), .width(4)) comparator_18 (
    .a(funct3_type), .b(4'b0110), .eq(comparator_18_eq));  // open: gt, lt
  Comparator #(.mode("unsigned"), .width(4)) comparator_19 (
    .a(funct3_type), .b(4'b0111), .eq(comparator_19_eq));  // open: gt, lt
  Priority_Encoder #(.select(4)) priority_encoder_1 (
    .in0(ALUSel_0), .in1(ALUSel_1), .in2(ALUSel_2), .in4(ALUSel_4), .in5(ALUSel_5), .in6(ALUSel_6),
    .in7(ALUSel_7), .in8(ALUSel_8), .in9(ALUSel_9), .in11(ALUSel_11), .in12(ALUSel_12), .in13(ALUSel_13),
    .out(ALUSel_imm));  // open: in3, in10, in14, in15, gs, en_out, en_in
  Multiplexer #(.enable("false"), .select(4), .width(4)) multiplexer_1 (
    .in0(ALUSel_type0), .in1(4'b0000), .in2(ALUSel_type1), .in3(4'b0000), .in4(4'b0000), .in5(4'b0000),
    .in6(4'b0000), .in7(4'b0000), .in8(4'b0000), .in9(4'b0000), .in10(4'b0000), .out(ALUSel),
    .sel(opcode_type));  // open: in11, in12, in13, in14, in15
  Multiplexer #(.enable("false"), .width(4)) multiplexer_2 (
    .in0(4'b1000), .in1(4'b0000), .out(multiplexer_2_out), .sel(comparator_1_eq));
  Multiplexer #(.enable("false"), .width(4)) multiplexer_3 (
    .in0(multiplexer_2_out), .in1(4'b0001), .out(multiplexer_3_out), .sel(comparator_2_eq));
  Multiplexer #(.enable("false"), .width(4)) multiplexer_4 (
    .in0(multiplexer_3_out), .in1(4'b0010), .out(multiplexer_4_out), .sel(comparator_3_eq));
  Multiplexer #(.enable("false"), .width(4)) multiplexer_5 (
    .in0(multiplexer_4_out), .in1(4'b0011), .out(multiplexer_5_out), .sel(comparator_4_eq));
  Multiplexer #(.enable("false"), .width(4)) multiplexer_6 (
    .in0(multiplexer_5_out), .in1(4'b0100), .out(multiplexer_6_out), .sel(comparator_5_eq));
  Multiplexer #(.enable("false"), .width(4)) multiplexer_7 (
    .in0(multiplexer_6_out), .in1(4'b0101), .out(multiplexer_7_out), .sel(comparator_6_eq));
  Multiplexer #(.enable("false"), .width(4)) multiplexer_8 (
    .in0(multiplexer_7_out), .in1(4'b0110), .out(multiplexer_8_out), .sel(comparator_7_eq));
  Multiplexer #(.enable("false"), .width(4)) multiplexer_9 (
    .in0(multiplexer_8_out), .in1(4'b0111), .out(funct3_type), .sel(comparator_8_eq));
  and and_1 (ALUSel_0, comparator_9_eq, comparator_10_eq);
  and and_2 (ALUSel_8, comparator_10_eq, comparator_11_eq);
  and and_3 (ALUSel_12, comparator_12_eq, comparator_10_eq);
  and and_4 (ALUSel_1, comparator_13_eq, comparator_9_eq);
  and and_5 (ALUSel_9, comparator_13_eq, comparator_11_eq);
  and and_6 (ALUSel_2, comparator_9_eq, comparator_14_eq);
  and and_7 (ALUSel_11, comparator_11_eq, comparator_15_eq);
  and and_8 (ALUSel_4, comparator_9_eq, comparator_16_eq);
  and and_9 (ALUSel_5, comparator_9_eq, comparator_17_eq);
  and and_10 (ALUSel_13, comparator_12_eq, comparator_17_eq);
  and and_11 (ALUSel_6, comparator_9_eq, comparator_18_eq);
  and and_12 (ALUSel_7, comparator_9_eq, comparator_19_eq);

  // Other names for the same wires on the sheet: funct7_imm[3:0] = {funct7[5:3], funct7[0]}

  // Notes on the sheet:
  //   INPUT
  //   All instructions except some R-type and I-type have ALUSel = 0(add) 
  //   OUTPUT
endmodule

module CSR (
  input  [3:0] opcode_type,
  input  [2:0] funct3,
  output CSRWen,
  output CSRSel
);

  wire multiplexer_1_out;

  Multiplexer #(.enable("false"), .select(3)) multiplexer_1 (
    .in0(1'b0), .in1(1'b0), .in2(1'b0), .in3(1'b0), .in4(1'b0), .in5(1'b1), .in6(1'b1), .in7(1'b1),
    .out(multiplexer_1_out), .sel(funct3));
  Multiplexer #(.enable("false"), .select(4)) multiplexer_2 (
    .in0(1'b0), .in1(1'b0), .in2(1'b0), .in3(1'b0), .in4(1'b0), .in5(1'b0), .in6(1'b0), .in7(1'b0),
    .in8(1'b0), .in9(1'b1), .in10(1'b0), .out(CSRWen), .sel(opcode_type));  // open: in11, in12, in13, in14, in15
  Multiplexer #(.enable("false"), .select(4)) multiplexer_3 (
    .in0(multiplexer_1_out), .in1(multiplexer_1_out), .in2(multiplexer_1_out), .in3(multiplexer_1_out),
    .in4(multiplexer_1_out), .in5(multiplexer_1_out), .in6(multiplexer_1_out), .in7(multiplexer_1_out),
    .in8(multiplexer_1_out), .in9(multiplexer_1_out), .in10(multiplexer_1_out), .out(CSRSel),
    .sel(opcode_type));  // open: in11, in12, in13, in14, in15

  // Notes on the sheet:
  //   INPUT
  //   OUTPUT
endmodule

module Mem (
  input  [3:0] opcode_type,
  output MemRW,
  output RegWEn
);

  Multiplexer #(.enable("false"), .select(4)) multiplexer_1 (
    .in0(1'b0), .in1(1'b0), .in2(1'b0), .in3(1'b1), .in4(1'b0), .in5(1'b0), .in6(1'b0), .in7(1'b0),
    .in8(1'b0), .in9(1'b0), .in10(1'b0), .out(MemRW), .sel(opcode_type));  // open: in11, in12, in13, in14, in15
  Multiplexer #(.enable("false"), .select(4)) multiplexer_2 (
    .in0(1'b1), .in1(1'b1), .in2(1'b1), .in3(1'b0), .in4(1'b0), .in5(1'b1), .in6(1'b1), .in7(1'b1),
    .in8(1'b1), .in9(1'b1), .in10(1'b0), .out(RegWEn), .sel(opcode_type));  // open: in11, in12, in13, in14, in15

  // Notes on the sheet:
  //   INPUT
  //   OUTPUT
endmodule

module Branch (
  input  [3:0] opcode_type,
  input  [2:0] funct3,
  input  BrEq,
  input  BrLt,
  output BrUn,
  output [1:0] PCSel
);

  wire multiplexer_1_out, multiplexer_2_out, not_1_out, not_2_out;
  wire [1:0] bit_extender_1_out;

  not not_1 (not_1_out, BrEq);
  not not_2 (not_2_out, BrLt);
  Multiplexer #(.enable("false"), .select(3)) multiplexer_1 (
    .in0(BrEq), .in1(not_1_out), .in4(BrLt), .in5(not_2_out), .in6(BrLt), .in7(not_2_out),
    .out(multiplexer_1_out), .sel(funct3));  // open: in2, in3
  assign bit_extender_1_out = {{1{1'b0}}, multiplexer_1_out};  // Bit_Extender bit_extender_1
  Multiplexer #(.enable("false"), .select(3)) multiplexer_2 (
    .in0(1'b0), .in1(1'b0), .in2(1'b0), .in3(1'b0), .in4(1'b0), .in5(1'b0), .in6(1'b1), .in7(1'b1),
    .out(multiplexer_2_out), .sel(funct3));
  Multiplexer #(.enable("false"), .select(4)) multiplexer_3 (
    .in0(1'b0), .in1(1'b0), .in2(1'b0), .in3(1'b0), .in4(multiplexer_2_out), .in5(1'b0), .in6(1'b0),
    .in7(1'b0), .in8(1'b0), .in9(1'b0), .in10(1'b0), .out(BrUn), .sel(opcode_type));  // open: in11, in12, in13, in14, in15
  Multiplexer #(.enable("false"), .select(4), .width(2)) multiplexer_4 (
    .in0(2'b00), .in1(2'b00), .in2(2'b00), .in3(2'b00), .in4(bit_extender_1_out), .in5(2'b00), .in6(2'b00),
    .in7(2'b01), .in8(2'b10), .in9(2'b00), .in10(2'b00), .out(PCSel), .sel(opcode_type));  // open: in11, in12, in13, in14, in15

  // Notes on the sheet:
  //   INPUT
  //   OUTPUT
endmodule

module ABSel (
  input  [3:0] opcode_type,
  output [1:0] ASel,
  output [1:0] BSel
);

  Multiplexer #(.enable("false"), .select(4), .width(2)) multiplexer_1 (
    .in0(2'b00), .in1(2'b00), .in2(2'b00), .in3(2'b00), .in4(2'b01), .in5(2'b01), .in6(2'b10), .in7(2'b01),
    .in8(2'b01), .in9(2'b00), .in10(2'b00), .out(ASel), .sel(opcode_type));  // open: in11, in12, in13, in14, in15
  Multiplexer #(.enable("false"), .select(4), .width(2)) multiplexer_2 (
    .in0(2'b00), .in1(2'b01), .in2(2'b01), .in3(2'b01), .in4(2'b00), .in5(2'b01), .in6(2'b01), .in7(2'b10),
    .in8(2'b10), .in9(2'b00), .in10(2'b00), .out(BSel), .sel(opcode_type));  // open: in11, in12, in13, in14, in15

  // Notes on the sheet:
  //   INPUT
  //   OUTPUT
endmodule

module WB (
  input  [3:0] opcode_type,
  output [1:0] WBSel
);

  Multiplexer #(.enable("false"), .select(4), .width(2)) multiplexer_1 (
    .in0(2'b00), .in1(2'b01), .in2(2'b00), .in3(2'b00), .in4(2'b00), .in5(2'b00), .in6(2'b00), .in7(2'b00),
    .in8(2'b00), .in9(2'b10), .in10(2'b00), .out(WBSel), .sel(opcode_type));  // open: in11, in12, in13, in14, in15

  // Notes on the sheet:
  //   INPUT
  //   OUTPUT
endmodule
