// Logisim project cpu.circ as structural Verilog: 1 circuit, main circuit cpu
module cpu (
  input  clk,
  input  [31:0] INSTRUCTION,
  input  [31:0] READ_DATA,
  output [31:0] WRITE_ADDRESS,
  output [31:0] PROGRAM_COUNTER,
  output [31:0] ra,
  output [31:0] sp,
  output [31:0] t0,
  output [31:0] t1,
  output [31:0] t2,
  output [31:0] s0,
  output [31:0] s1,
  output [31:0] a0,
  output [31:0] tohost,
  output [3:0] WRITE_ENABLE,
  output [31:0] WRITE_DATA
);

  wire BrEq, BrLt, BrUn, CSRSel, CSRWen, MemRW, RegWEn;
  wire [1:0] ASel, BSel, PCSel, WBSel;
  wire [2:0] funct3, ImmSel;
  wire [3:0] ALUSel, multiplexer_8_out, multiplexer_9_out, multiplexer_10_out;
  wire [4:0] bit_extender_2_out, bit_extender_3_out, multiplier_1_out, multiplier_2_out;
  wire [11:0] csr_addr;
  wire [19:0] inst_id;
  wire [31:0] adder_1_out, adder_2_out, bit_extender_1_out, bit_extender_4_out, bit_extender_5_out,
       bit_extender_6_out, bit_extender_7_out, imm, multiplexer_1_out, multiplexer_2_out, multiplexer_5_out,
       multiplexer_6_out, multiplexer_7_out, multiplexer_13_out, pc_4, pc_id, register_1_q, register_2_q,
       rs1_data, rs2_data, shifter_1_out, shifter_2_out, shifter_3_out, shifter_4_out, WB_Data;

  Adder #(.width(32)) adder_1 (.a(pc_id), .b(imm), .out(adder_1_out));  // open: cin, cout
  Adder #(.width(32)) adder_2 (.a(rs1_data), .b(imm), .out(adder_2_out));  // open: cin, cout
  Multiplexer #(.enable("false"), .select(2), .width(32)) multiplexer_1 (
    .in0(INSTRUCTION), .in1(32'h13), .in2(32'h13), .in3(32'h13), .out(multiplexer_1_out), .sel(PCSel));
  Register #(.width(32)) register_1 (.D(PROGRAM_COUNTER), .en(1'b1), .clk(clk), .Q(register_1_q));  // open: clr
  Register #(.width(32)) register_2 (.D(multiplexer_1_out), .en(1'b1), .clk(clk), .Q(register_2_q));  // open: clr
  Multiplexer #(.enable("false"), .select(2), .width(32)) multiplexer_2 (
    .in0(pc_4), .in1(adder_1_out), .in2(adder_2_out), .out(multiplexer_2_out), .sel(PCSel));  // open: in3
  Register #(.width(32)) PC (.D(multiplexer_2_out), .en(1'b1), .clk(clk), .Q(PROGRAM_COUNTER));  // open: clr
  Multiplexer #(.enable("false"), .width(32)) multiplexer_3 (
    .in0(PROGRAM_COUNTER), .in1(register_1_q), .out(pc_id), .sel(1'b1));
  Multiplexer #(.enable("false"), .width(32)) multiplexer_4 (
    .in0(INSTRUCTION), .in1(register_2_q), .out({csr_addr, inst_id[19:15], funct3, inst_id[11:0]}), .sel(1'b1));
  Adder #(.width(32)) adder_3 (.a(PROGRAM_COUNTER), .b(32'h4), .out(pc_4));  // open: cin, cout
  // branch_comp branch_comp_1: pin names not known; wires that end beside it: rs1_data, rs2_data, BrUn, BrEq, BrLt
  imm_gen imm_gen_1 (.inst({csr_addr, inst_id[19:15], funct3, inst_id[11:0]}), .ImmSel(ImmSel), .imm(imm));
  control_logic control_logic_1 (
    .CSRWen(CSRWen), .PCSel(PCSel), .RegWEn(RegWEn), .ImmSel(ImmSel), .BrUn(BrUn), .ASel(ASel), .BSel(BSel),
    .ALUSel(ALUSel), .MemRW(MemRW), .WBSel(WBSel), .CSRSel(CSRSel),
    .inst({csr_addr, inst_id[19:15], funct3, inst_id[11:0]}), .BrEq(BrEq), .BrLt(BrLt));
  Multiplexer #(.enable("false"), .select(2), .width(32)) multiplexer_5 (
    .in0(rs1_data), .in1(pc_id), .in2({32{1'b0}}), .out(multiplexer_5_out), .sel(ASel));  // open: in3
  Multiplexer #(.enable("false"), .select(2), .width(32)) multiplexer_6 (
    .in0(rs2_data), .in1(imm), .in2(32'h4), .out(multiplexer_6_out), .sel(BSel));  // open: in3
  // alu alu_1: pin names not known; wires that end beside it: multiplexer_5_out, multiplexer_6_out, ALUSel, WRITE_ADDRESS
  // regfile regfile_1: pin names not known; wires that end beside it: inst_id[19:15], csr_addr[4:0], inst_id[11:7], WB_Data, RegWEn, clk, ra, sp, t0, t1, t2, s0, s1, a0, rs1_data, rs2_data
  Multiplexer #(.enable("false"), .width(32)) multiplexer_7 (
    .in0(rs1_data), .in1(bit_extender_1_out), .out(multiplexer_7_out), .sel(CSRSel));
  assign bit_extender_1_out = {{27{1'b0}}, inst_id[19:15]};  // Bit_Extender bit_extender_1
  // csr csr_1: pin names not known; wires that end beside it: csr_addr, multiplexer_7_out, CSRWen, clk, tohost
  assign bit_extender_2_out = {{3{1'b0}}, WRITE_ADDRESS[1:0]};  // Bit_Extender bit_extender_2
  assign bit_extender_3_out = {{3{1'b0}}, WRITE_ADDRESS[1:0]};  // Bit_Extender bit_extender_3
  Multiplier #(.width(5)) multiplier_1 (
    .a(bit_extender_2_out), .b(5'b01000), .out(multiplier_1_out));  // open: cin, cout
  Multiplier #(.width(5)) multiplier_2 (
    .a(bit_extender_3_out), .b(5'b01000), .out(multiplier_2_out));  // open: cin, cout
  Multiplexer #(.enable("false"), .select(2), .width(4)) multiplexer_8 (
    .in0(4'b0001), .in1(4'b0010), .in2(4'b0100), .in3(4'b1000), .out(multiplexer_8_out),
    .sel(WRITE_ADDRESS[1:0]));
  Multiplexer #(.enable("false"), .select(2), .width(4)) multiplexer_9 (
    .in0(4'b0011), .in1(4'b0110), .in2(4'b1100), .in3(4'b0000), .out(multiplexer_9_out),
    .sel(WRITE_ADDRESS[1:0]));
  assign bit_extender_4_out = {{24{1'b0}}, rs2_data[7:0]};  // Bit_Extender bit_extender_4
  assign bit_extender_5_out = {{16{1'b0}}, rs2_data[15:0]};  // Bit_Extender bit_extender_5
  Shifter #(.shift("lr"), .width(32)) shifter_1 (.in(READ_DATA), .\dist (multiplier_1_out), .out(shifter_1_out));
  Shifter #(.shift("lr"), .width(32)) shifter_2 (.in(READ_DATA), .\dist (multiplier_1_out), .out(shifter_2_out));
  Multiplexer #(.enable("false"), .select(3), .width(4)) multiplexer_10 (
    .in0(multiplexer_8_out), .in1(multiplexer_9_out), .in2(4'b1111), .out(multiplexer_10_out), .sel(funct3));  // open: in3, in4, in5, in6, in7
  Shifter #(.width(32)) shifter_3 (.in(bit_extender_4_out), .\dist (multiplier_2_out), .out(shifter_3_out));
  Shifter #(.width(32)) shifter_4 (.in(bit_extender_5_out), .\dist (multiplier_2_out), .out(shifter_4_out));
  assign bit_extender_6_out = {{24{shifter_1_out[7]}}, shifter_1_out[7:0]};  // Bit_Extender bit_extender_6
  assign bit_extender_7_out = {{16{shifter_2_out[15]}}, shifter_2_out[15:0]};  // Bit_Extender bit_extender_7
  Multiplexer #(.enable("false"), .width(4)) multiplexer_11 (
    .in0(4'b0000), .in1(multiplexer_10_out), .out(WRITE_ENABLE), .sel(MemRW));
  Multiplexer #(.enable("false"), .select(3), .width(32)) multiplexer_12 (
    .in0(shifter_3_out), .in1(shifter_4_out), .in2(rs2_data), .out(WRITE_DATA), .sel(funct3));  // open: in3, in4, in5, in6, in7
  Multiplexer #(.enable("false"), .select(3), .width(32)) multiplexer_13 (
    .in0(bit_extender_6_out), .in1(bit_extender_7_out), .in2(READ_DATA), .out(multiplexer_13_out),
    .sel(funct3));  // open: in3, in4, in5, in6, in7
  Multiplexer #(.enable("false"), .select(2), .width(32)) multiplexer_14 (
    .in0(WRITE_ADDRESS), .in1(multiplexer_13_out), .in2(tohost), .out(WB_Data), .sel(WBSel));  // open: in3

  // Other names for the same wires on the sheet: ALU_out[31:0] = WRITE_ADDRESS; mem_addr[1:0] = WRITE_ADDRESS[1:0];
  //   opcode[6:0] = inst_id[6:0]; rd[4:0] = inst_id[11:7]; inst_id (some bits) = {csr_addr, funct3};
  //   rs1[4:0] = inst_id[19:15]; rs2[4:0] = csr_addr[4:0]

  // Notes on the sheet:
  //   Output to IMEM
  //   IMEM (do **NOT** move this)
  //   Inputs from IMEM
  //   Inputs/Outputs for testing. Do **NOT** move these.
  //   Outputs To DMEM
  //   DMEM (do **NOT** move this)
  //   Inputs From DMEM
endmodule
