// Logisim project imm-gen.circ as structural Verilog: 1 circuit, main circuit imm_gen
module imm_gen (
  input  [31:0] inst,
  input  [2:0] ImmSel,
  output [31:0] imm
);

  wire [31:0] bit_extender_1_out, bit_extender_2_out, bit_extender_3_out, bit_extender_4_out,
       bit_extender_5_out, bit_extender_6_out, bit_extender_7_out, bit_extender_8_out, bit_extender_9_out,
       bit_extender_10_out, bit_extender_11_out, bit_extender_12_out, or_1_out, or_2_out, or_3_out,
       shifter_1_out, shifter_2_out, shifter_3_out, shifter_4_out, shifter_5_out, shifter_6_out,
       shifter_7_out, shifter_8_out, shifter_9_out, shifter_10_out;

  assign bit_extender_1_out = {{27{1'b0}}, inst[11:7]};  // Bit_Extender bit_extender_1
  assign bit_extender_2_out = {{25{inst[31]}}, inst[31:25]};  // Bit_Extender bit_extender_2
  assign bit_extender_3_out = {{31{1'b0}}, inst[7]};  // Bit_Extender bit_extender_3
  assign bit_extender_4_out = {{28{1'b0}}, inst[11:8]};  // Bit_Extender bit_extender_4
  assign bit_extender_5_out = {{26{1'b0}}, inst[30:25]};  // Bit_Extender bit_extender_5
  assign bit_extender_6_out = {{31{inst[31]}}, inst[31]};  // Bit_Extender bit_extender_6
  assign bit_extender_7_out = {{12{inst[31]}}, inst[31:12]};  // Bit_Extender bit_extender_7
  assign bit_extender_8_out = {{24{1'b0}}, inst[19:12]};  // Bit_Extender bit_extender_8
  assign bit_extender_9_out = {{31{1'b0}}, inst[20]};  // Bit_Extender bit_extender_9
  assign bit_extender_10_out = {{22{1'b0}}, inst[30:21]};  // Bit_Extender bit_extender_10
  assign bit_extender_11_out = {{31{inst[31]}}, inst[31]};  // Bit_Extender bit_extender_11
  assign bit_extender_12_out = {{20{inst[31]}}, inst[31:20]};  // Bit_Extender bit_extender_12
  Shifter #(.width(32)) shifter_1 (.in(bit_extender_2_out), .\dist (5'b00101), .out(shifter_1_out));
  Shifter #(.width(32)) shifter_2 (.in(bit_extender_3_out), .\dist (5'b01011), .out(shifter_2_out));
  Shifter #(.width(32)) shifter_3 (.in(bit_extender_4_out), .\dist (5'b00001), .out(shifter_3_out));
  Shifter #(.width(32)) shifter_4 (.in(bit_extender_5_out), .\dist (5'b00101), .out(shifter_4_out));
  Shifter #(.width(32)) shifter_5 (.in(bit_extender_6_out), .\dist (5'b01100), .out(shifter_5_out));
  Shifter #(.width(32)) shifter_6 (.in(bit_extender_7_out), .\dist (5'b01100), .out(shifter_6_out));
  Shifter #(.width(32)) shifter_7 (.in(bit_extender_8_out), .\dist (5'b01100), .out(shifter_7_out));
  Shifter #(.width(32)) shifter_8 (.in(bit_extender_9_out), .\dist (5'b01011), .out(shifter_8_out));
  Shifter #(.width(32)) shifter_9 (.in(bit_extender_10_out), .\dist (5'b00001), .out(shifter_9_out));
  Shifter #(.width(32)) shifter_10 (.in(bit_extender_11_out), .\dist (5'b10100), .out(shifter_10_out));
  assign or_1_out = bit_extender_1_out | shifter_1_out;  // OR_Gate or_1, 32 bits wide
  assign or_2_out = shifter_2_out | shifter_3_out | shifter_4_out | shifter_5_out;  // OR_Gate or_2, 32 bits wide
  assign or_3_out = shifter_7_out | shifter_8_out | shifter_9_out | shifter_10_out;  // OR_Gate or_3, 32 bits wide
  Multiplexer #(.enable("false"), .select(3), .width(32)) multiplexer_1 (
    .in0(bit_extender_12_out), .in1(or_1_out), .in2(or_2_out), .in3(shifter_6_out), .in4(or_3_out),
    .out(imm), .sel(ImmSel));  // open: in5, in6, in7

  // Notes on the sheet:
  //   INPUTS to your circuit
  //   DON'T CHANGE THE LOCATIONS OF THE INPUTS AND OUTPUTS!
  //   OUTPUT from your circuit
endmodule
